// Digital circuit TGI_07_RS-Latch.dig as structural Verilog
module TGI_07_RS_Latch (
  input  R,
  input  S,
  input  S_2,
  input  R_2,
  output Q,
  output Q_2,
  output Q_3,
  output Q_4
);

  wire not_1_out, not_2_out;

  nor nor_1 (Q, R, Q_2);
  nor nor_2 (Q_2, Q, S);
  nand nand_1 (Q_3, not_1_out, Q_4);
  not not_1 (not_1_out, S_2);
  nand nand_2 (Q_4, Q_3, not_2_out);
  not not_2 (not_2_out, R_2);
endmodule
