// Digital circuit Ampel.dig as structural Verilog
module Ampel (
  input  X,
  input  Clock
);

  wire and_1_out, and_2_out, and_3_out, and_4_out, and_5_out, and_6_out, and_7_out, and_8_out, and_9_out,
       not_1_out, or_1_out, or_2_out, or_3_out, or_4_out, or_5_out, or_6_out, Q0_q, Q1_q, Q2_q;

  D_FF Q2 (.D(or_5_out), .C(Clock), .Q(Q2_q));  // open: nQ
  and and_1 (and_1_out, Q1_q, Q0_q);
  or or_1 (or_1_out, Q1_q, Q2_q);
  and and_2 (and_2_out, Q0_q, ~Q1_q);  // And
  and and_3 (and_3_out, ~X, Q0_q, Q1_q);  // And
  and and_4 (and_4_out, ~Q0_q, Q2_q);  // And
  and and_5 (and_5_out, ~Q0_q, Q1_q);  // And
  and and_6 (and_6_out, X, Q1_q);
  and and_7 (and_7_out, Q0_q, ~Q1_q, ~Q2_q);  // And
  or or_2 (or_2_out, ~Q0_q, Q1_q);  // Or
  or or_3 (or_3_out, ~Q0_q, X);  // Or
  or or_4 (or_4_out, X, Q1_q, Q2_q);
  D_FF Q1 (.D(or_6_out), .C(Clock), .Q(Q1_q));  // open: nQ
  not not_1 (not_1_out, and_1_out);
  and and_8 (and_8_out, ~or_1_out, ~and_2_out);  // And
  or or_5 (or_5_out, and_3_out, and_4_out);
  or or_6 (or_6_out, and_5_out, and_6_out, and_7_out);
  and and_9 (and_9_out, or_2_out, or_3_out, or_4_out);
  LED \Fußgänger_rot  (.in(not_1_out));
  LED \Fußgänger_gruen  (.in(and_1_out));
  LED Auto_rot (.in(or_1_out));
  LED Auto_gelb (.in(and_2_out));
  LED Auto_gruen (.in(and_8_out));
  D_FF Q0 (.D(and_9_out), .C(Clock), .Q(Q0_q));  // open: nQ

  // Notes on the sheet:
  //   Fußgänger
  //   Auto
  //   Q_2^'
  //   Q_1^'
  //   Q_0^'
endmodule
