// Digital circuit 08_A_Automaten_Aufgabe-1.dig as structural Verilog
module _08_A_Automaten_Aufgabe_1 (
  input  Cock,
  input  X,
  input  Cock_2,
  input  X_2,
  output Y,
  output Y_2
);

  wire and_1_out, and_2_out, and_3_out, and_4_out, and_5_out, and_6_out, and_7_out, and_8_out, and_9_out,
       and_10_out, and_11_out, and_12_out, and_13_out, d_ff_1_q, d_ff_2_q, d_ff_3_q, d_ff_4_q, or_1_out,
       or_2_out, or_3_out, or_4_out, or_6_out, or_8_out;

  D_FF d_ff_1 (.D(and_12_out), .C(Cock), .Q(d_ff_1_q));  // open: nQ
  D_FF d_ff_2 (.D(or_6_out), .C(Cock), .Q(d_ff_2_q));  // open: nQ
  D_FF d_ff_3 (.D(or_8_out), .C(Cock_2), .Q(d_ff_3_q));  // open: nQ
  D_FF d_ff_4 (.D(and_13_out), .C(Cock_2), .Q(d_ff_4_q));  // open: nQ
  and and_1 (and_1_out, X_2, ~d_ff_4_q);  // And
  and and_2 (and_2_out, d_ff_4_q, ~d_ff_3_q);  // And
  or or_1 (or_1_out, ~d_ff_3_q, d_ff_4_q, ~X_2);  // Or
  or or_2 (or_2_out, d_ff_3_q, ~d_ff_4_q, X_2);  // Or
  and and_3 (and_3_out, ~d_ff_1_q, ~d_ff_2_q, X);  // And
  and and_4 (and_4_out, d_ff_1_q, ~X);  // And
  and and_5 (and_5_out, d_ff_2_q, d_ff_1_q);
  or or_3 (or_3_out, d_ff_1_q, d_ff_2_q, X);
  or or_4 (or_4_out, ~d_ff_1_q, d_ff_2_q, ~X);  // Or
  and and_6 (and_6_out, ~d_ff_1_q, ~X);  // And
  and and_7 (and_7_out, ~d_ff_1_q, ~d_ff_2_q);  // And
  and and_8 (and_8_out, ~d_ff_2_q, ~X);  // And
  and and_9 (and_9_out, ~d_ff_3_q, ~d_ff_4_q, X_2);  // And
  and and_10 (and_10_out, d_ff_3_q, ~X_2);  // And
  and and_11 (and_11_out, d_ff_4_q, d_ff_3_q);
  or or_5 (Y, and_3_out, and_4_out, and_5_out);
  and and_12 (and_12_out, or_3_out, or_4_out);
  or or_6 (or_6_out, and_6_out, and_7_out, and_8_out);
  or or_7 (Y_2, and_9_out, and_10_out, and_11_out);
  or or_8 (or_8_out, and_1_out, and_2_out);
  and and_13 (and_13_out, or_1_out, or_2_out);

  // Notes on the sheet:
  //   Mit D-FlipFlops
  //   S_0
  //   S_1
  //   Mit T-FlipFlops
  //   Übergangsfunktion T_0^'
  //   Übergangsfunktion T_1^'
  //   Ausgabefunktion
  //   Übergangsfunktion S_0^'
  //   Übergangsfunktion S_1^'
endmodule
