// Digital circuit Zaehler_0-9_Dezimal_LED.dig as structural Verilog
module Zaehler_0_9_Dezimal_LED (
  input  Cock,
  output q_3,
  output q_2,
  output q_1,
  output q_0
);

  wire and_1_out, and_2_out, and_3_out, and_4_out, and_5_out, and_6_out, and_7_out, and_8_out, and_9_out,
       not_1_out, or_1_out, or_2_out, or_3_out, or_4_out;

  and and_1 (and_1_out, q_0, q_1, q_2);
  and and_2 (and_2_out, ~q_0, q_3);  // And
  and and_3 (and_3_out, ~q_1, q_2);  // And
  and and_4 (and_4_out, ~q_0, q_2);  // And
  and and_5 (and_5_out, q_0, q_1, ~q_2);  // And
  and and_6 (and_6_out, q_0, ~q_1, ~q_3);  // And
  and and_7 (and_7_out, ~q_0, q_1);  // And
  not not_1 (not_1_out, q_0);
  LED u_q_3 (.in(q_3));
  LED u_q_2 (.in(q_2));
  or or_1 (or_1_out, and_1_out, and_2_out);
  or or_2 (or_2_out, and_3_out, and_4_out, and_5_out);
  or or_3 (or_3_out, and_6_out, and_7_out);
  LED u_q_1 (.in(q_1));
  LED u_q_0 (.in(q_0));
  D_FF_AS d_ff_as_1 (.Set(1'b0), .D(or_1_out), .C(Cock), .Clr(1'b0), .Q(q_3));  // open: nQ
  D_FF_AS d_ff_as_2 (.Set(1'b0), .D(or_2_out), .C(Cock), .Clr(1'b0), .Q(q_2));  // open: nQ
  D_FF_AS d_ff_as_3 (.Set(1'b0), .D(or_3_out), .C(Cock), .Clr(1'b0), .Q(q_1));  // open: nQ
  D_FF_AS d_ff_as_4 (.Set(1'b0), .D(not_1_out), .C(Cock), .Clr(1'b0), .Q(q_0));  // open: nQ
  and and_8 (and_8_out, ~q_0, q_2, q_1);  // And
  and and_9 (and_9_out, q_0, q_3);
  or or_4 (or_4_out, and_8_out, and_9_out);
  Seven_Seg_Hex seven_seg_hex_1 (.d({q_3, q_2, q_1, q_0}), .dp(or_4_out));

  // Notes on the sheet:
  //   Übergangsschaltnetz für q_3'
  //   Übergangsschaltnetz für q_2'
  //   Übergangsschaltnetz für q_1'
  //   Übergangsschaltnetz für q_0'
  //   Punkt für 6 und 9 (nice)
endmodule
