// Digital circuit 8-Bit-ALU.dig as structural Verilog
module _8_Bit_ALU (
  input  INVA,
  input  [7:0] A,
  input  ENA,
  input  [7:0] B,
  input  ENB,
  input  C_IN,
  input  F0,
  input  F1,
  output C_OUT,
  output [7:0] OUT
);

  wire _1_bit_alu_1_c_out, _1_bit_alu_2_c_out, _1_bit_alu_3_c_out, _1_bit_alu_4_c_out, _1_bit_alu_5_c_out,
       _1_bit_alu_6_c_out, _1_bit_alu_7_c_out;

  _1_Bit_ALU _1_bit_alu_1 (
    .INVA(INVA), .A(A[0]), .ENA(ENA), .B(B[0]), .ENB(ENB), .C_IN(C_IN), .F0(F0), .F1(F1),
    .C_OUT(_1_bit_alu_1_c_out), .OUT(OUT[0]));
  _1_Bit_ALU _1_bit_alu_2 (
    .INVA(INVA), .A(A[1]), .ENA(ENA), .B(B[1]), .ENB(ENB), .C_IN(_1_bit_alu_1_c_out), .F0(F0), .F1(F1),
    .C_OUT(_1_bit_alu_2_c_out), .OUT(OUT[1]));
  _1_Bit_ALU _1_bit_alu_3 (
    .INVA(INVA), .A(A[2]), .ENA(ENA), .B(B[2]), .ENB(ENB), .C_IN(_1_bit_alu_2_c_out), .F0(F0), .F1(F1),
    .C_OUT(_1_bit_alu_3_c_out), .OUT(OUT[2]));
  _1_Bit_ALU _1_bit_alu_4 (
    .INVA(INVA), .A(A[3]), .ENA(ENA), .B(B[3]), .ENB(ENB), .C_IN(_1_bit_alu_3_c_out), .F0(F0), .F1(F1),
    .C_OUT(_1_bit_alu_4_c_out), .OUT(OUT[3]));
  _1_Bit_ALU _1_bit_alu_5 (
    .INVA(INVA), .A(A[4]), .ENA(ENA), .B(B[4]), .ENB(ENB), .C_IN(_1_bit_alu_4_c_out), .F0(F0), .F1(F1),
    .C_OUT(_1_bit_alu_5_c_out), .OUT(OUT[4]));
  _1_Bit_ALU _1_bit_alu_6 (
    .INVA(INVA), .A(A[5]), .ENA(ENA), .B(B[5]), .ENB(ENB), .C_IN(_1_bit_alu_5_c_out), .F0(F0), .F1(F1),
    .C_OUT(_1_bit_alu_6_c_out), .OUT(OUT[5]));
  _1_Bit_ALU _1_bit_alu_7 (
    .INVA(INVA), .A(A[6]), .ENA(ENA), .B(B[6]), .ENB(ENB), .C_IN(_1_bit_alu_6_c_out), .F0(F0), .F1(F1),
    .C_OUT(_1_bit_alu_7_c_out), .OUT(OUT[6]));
  _1_Bit_ALU _1_bit_alu_8 (
    .INVA(INVA), .A(A[7]), .ENA(ENA), .B(B[7]), .ENB(ENB), .C_IN(_1_bit_alu_7_c_out), .F0(F0), .F1(F1),
    .C_OUT(C_OUT), .OUT(OUT[7]));
endmodule
