// Digital circuit Vorbreitung_Komplettrechner.dig as structural Verilog
module Vorbreitung_Komplettrechner (
  input  Clock,
  input  RST
);

  wire and_1_out, not_1_out, not_2_out, or_1_out, sequencer_1_execute, sequencer_1_fetch_dr,
       sequencer_1_fetch_ir;
  wire [6:0] programcounter_1_a_out;
  wire [7:0] _8_bit_alu_1_out, Akku_d_out, DR_d_out, IR_d_out, rom_1_d;
  wire [7:7] programcounter_1_a_out_2;

  not not_1 (not_1_out, Clock);
  Sequencer sequencer_1 (
    .CLK(not_1_out), .RST(RST), .FETCH_IR(sequencer_1_fetch_ir), .FETCH_DR(sequencer_1_fetch_dr),
    .EXECUTE(sequencer_1_execute));
  or or_1 (or_1_out, sequencer_1_fetch_ir, sequencer_1_fetch_dr);
  and and_1 (and_1_out, or_1_out, Clock);
  _8_Bit_Register IR (.RST(1'b0), .EN(sequencer_1_fetch_ir), .D_in(rom_1_d), .CLK(Clock), .D_out(IR_d_out));
  Seven_Seg_Hex seven_seg_hex_1 (.d(IR_d_out[7:4]), .dp(1'b1));
  ProgramCounter programcounter_1 (
    .A_IN({8{1'b0}}), .INC(1'b1), .EN(1'b1), .CLK(and_1_out), .RST(RST),
    .A_OUT({programcounter_1_a_out_2[7], programcounter_1_a_out}));
  Seven_Seg_Hex seven_seg_hex_2 (.d(IR_d_out[3:0]), .dp(1'b1));
  not not_2 (not_2_out, programcounter_1_a_out_2[7]);
  _8_Bit_Register DR (.RST(1'b0), .EN(sequencer_1_fetch_dr), .D_in(rom_1_d), .CLK(Clock), .D_out(DR_d_out));
  ROM #(.AddrBits(7), .Bits(8)) rom_1 (.A(programcounter_1_a_out), .sel(not_2_out), .D(rom_1_d));
  RAMDualPort #(.AddrBits(7), .Bits(8)) ramdualport_1 (
    .A(programcounter_1_a_out), .Din({8{1'b0}}), .str(1'b0), .C(Clock), .ld(programcounter_1_a_out_2[7]),
    .D(rom_1_d));
  Seven_Seg_Hex seven_seg_hex_3 (.d(DR_d_out[7:4]), .dp(1'b1));
  Seven_Seg_Hex seven_seg_hex_4 (.d(DR_d_out[3:0]), .dp(1'b1));
  _8_Bit_ALU _8_bit_alu_1 (
    .INVA(1'b0), .A(IR_d_out), .ENA(1'b1), .B(DR_d_out), .ENB(1'b1), .C_IN(1'b0), .F0(1'b1), .F1(1'b1),
    .OUT(_8_bit_alu_1_out));  // open: C_OUT
  _8_Bit_Register Akku (.RST(1'b0), .EN(sequencer_1_execute), .D_in(_8_bit_alu_1_out), .CLK(Clock), .D_out(Akku_d_out));
  Seven_Seg_Hex seven_seg_hex_5 (.d(Akku_d_out[7:4]), .dp(1'b1));
  Seven_Seg_Hex seven_seg_hex_6 (.d(Akku_d_out[3:0]), .dp(1'b1));

  // Other names for the same wires on the sheet: C = Clock

  // Notes on the sheet:
  //   Clock: Hz: 1000
  //   RST: Reset
  //   contents of rom_1 (hex, n*v repeats v):
  //   6,9,1,1
endmodule
