// Digital circuit ALU-Bus.dig as structural Verilog
module ALU_Bus (
  input  [4:0] CTRL,
  input  [7:0] A,
  input  [7:0] B,
  input  C_IN,
  output [7:0] OUT,
  output C_OUT
);

  _8_Bit_ALU _8_bit_alu_1 (
    .INVA(CTRL[0]), .A(A), .ENA(CTRL[1]), .B(B), .ENB(CTRL[2]), .C_IN(C_IN), .F0(CTRL[3]), .F1(CTRL[4]),
    .C_OUT(C_OUT), .OUT(OUT));
endmodule
