// Digital circuit garagentor.dig as structural Verilog
module garagentor (
  input  T_heben,
  input  T_oben,
  input  T_senken,
  input  T_unten,
  input  Lichtschranke,
  output M_heben,
  output M_senken
);

  and and_1 (M_heben, T_heben, ~T_senken, ~T_oben);  // And
  and and_2 (M_senken, T_senken, ~T_unten, ~T_heben, Lichtschranke);  // And
endmodule
