// Digital circuit 08_A_Automaten_Aufgabe-1.dig as structural Verilog
module _08_A_Automaten_Aufgabe_1 (
  input  Cock,
  input  X,
  output Y
);

  wire and_1_out, and_2_out, and_3_out, and_4_out, and_5_out, and_6_out, and_7_out, d_ff_1_q, d_ff_2_q,
       or_1_out, or_2_out, or_4_out;

  D_FF d_ff_1 (.D(and_7_out), .C(Cock), .Q(d_ff_1_q));  // open: nQ
  D_FF d_ff_2 (.D(or_4_out), .C(Cock), .Q(d_ff_2_q));  // open: nQ
  and and_1 (and_1_out, ~d_ff_1_q, ~d_ff_2_q, X);  // And
  and and_2 (and_2_out, d_ff_1_q, ~X);  // And
  and and_3 (and_3_out, d_ff_2_q, d_ff_1_q);
  or or_1 (or_1_out, d_ff_1_q, d_ff_2_q, X);
  or or_2 (or_2_out, ~d_ff_1_q, d_ff_2_q, ~X);  // Or
  and and_4 (and_4_out, ~d_ff_1_q, ~X);  // And
  and and_5 (and_5_out, ~d_ff_1_q, ~d_ff_2_q);  // And
  and and_6 (and_6_out, ~d_ff_2_q, ~X);  // And
  or or_3 (Y, and_1_out, and_2_out, and_3_out);
  and and_7 (and_7_out, or_1_out, or_2_out);
  or or_4 (or_4_out, and_4_out, and_5_out, and_6_out);

  // Notes on the sheet:
  //   S_0
  //   S_1
  //   Ausgabefunktion
  //   Übergangsfunktion S_0^'
  //   Übergangsfunktion S_1^'
endmodule
