// Digital circuit FlipFlopAmpel.dig as structural Verilog
module FlipFlopAmpel (
  input  in_1,
  input  in_2,
  input  in_3,
  input  in_6,
  input  clk,
  input  X,
  input  Clock,
  input  X_2,
  input  Clock_2,
  output out_4,
  output out_5,
  output Y2,
  output Y1,
  output Y0,
  output Q1,
  output Q2,
  output Y3,
  output Y2_2,
  output Y1_2,
  output Q3,
  output Q4,
  output \Fußgänger_Grün ,
  output \Fußgänger_Rot 
);

  wire and_1_out, and_2_out, and_3_out, and_4_out, and_5_out, and_6_out, or_1_out, or_2_out;

  xor xor_1 (Y2_2, Q3, Q4);
  nor nor_1 (Y1_2, Q3, Q4);
  and and_1 (and_1_out, Q4, X_2);
  and and_2 (and_2_out, Q4, ~Q3);  // And
  and and_3 (and_3_out, ~Q3, X_2);  // And
  D_FF d_ff_1 (.D(Q4), .C(Clock_2), .Q(Q3));  // open: nQ
  xor xor_2 (Y1, Q1, Q2);
  nor nor_2 (Y0, Q1, Q2);
  and and_4 (and_4_out, Q2, X);
  and and_5 (and_5_out, Q2, ~Q1);  // And
  and and_6 (and_6_out, ~Q1, X);  // And
  D_FF d_ff_2 (.D(Q2), .C(Clock), .Q(Q1));  // open: nQ
  or or_1 (or_1_out, and_1_out, and_2_out, and_3_out);
  or or_2 (or_2_out, and_4_out, and_5_out, and_6_out);
  D_FF_AS d_ff_as_1 (.Set(in_1), .D(in_2), .C(clk), .Clr(in_3), .Q(out_4), .nQ(out_5));
  and and_7 (\Fußgänger_Grün , Q3, ~Y2_2, ~Y1_2);  // And
  D_FF d_ff_3 (.D(or_1_out), .C(Clock_2), .Q(Q4));  // open: nQ
  not not_1 (\Fußgänger_Rot , \Fußgänger_Grün );
  D_FF d_ff_4 (.D(or_2_out), .C(Clock), .Q(Q2));  // open: nQ

  assign Y2 = Q1;
  assign Y3 = Q3;

  // Notes on the sheet:
  //   Aufgabe 3
  //   Aufgabe 1
  //   Aufgabe 2
endmodule
