// Digital circuit Sequencer.dig as structural Verilog
module Sequencer (
  input  CLK,
  input  RST,
  output FETCH_IR,
  output FETCH_DR,
  output EXECUTE
);

  wire and_1_out, d_ff_as_1_q, d_ff_as_2_q;

  D_FF_AS d_ff_as_1 (.Set(1'b0), .D(and_1_out), .C(CLK), .Clr(RST), .Q(d_ff_as_1_q));  // open: nQ
  and and_1 (and_1_out, ~d_ff_as_1_q, ~d_ff_as_2_q);  // And
  D_FF_AS d_ff_as_2 (.Set(1'b0), .D(d_ff_as_1_q), .C(CLK), .Clr(RST), .Q(d_ff_as_2_q));  // open: nQ
  and and_2 (FETCH_IR, ~d_ff_as_1_q, ~d_ff_as_2_q);  // And
  and and_3 (FETCH_DR, d_ff_as_1_q, ~d_ff_as_2_q);  // And
  and and_4 (EXECUTE, ~d_ff_as_1_q, d_ff_as_2_q);  // And

  // Notes on the sheet:
  //   CLK: Cock
  //   RST: Zurücksetz
  //   FETCH_IR: Fetch Instruction Register
  //   FETCH_DR: Fetch Data Register
  //   EXECUTE: Execute
  //   Übergangsschaltnetz für q_0'
  //   q_0
  //   q_1
  //   FIR-Logik
  //   FDR-Logik
  //   Execute-Logik
endmodule
