// Digital circuit 1_2_Mux_Demux.dig as structural Verilog
module _1_2_Mux_Demux (
  input  I1,
  input  I2,
  input  S,
  input  I,
  input  S_2,
  output O,
  output O1,
  output O2
);

  wire and_1_out, and_2_out;

  and and_1 (and_1_out, I1, ~S);  // And
  and and_2 (and_2_out, I2, S);
  and and_3 (O1, I, ~S_2);  // And
  and and_4 (O2, I, S_2);
  or or_1 (O, and_1_out, and_2_out);

  // Notes on the sheet:
  //   2:1 Multiplexer
  //   1:2 Demultiplexer
endmodule
