// Digital circuit Memory_ROM_RAM.dig as structural Verilog
module Memory_ROM_RAM (
  input  [7:0] Addr,
  input  D_in,
  input  str,
  input  C,
  output [7:0] D_out
);

  wire not_1_out;
  wire [7:7] undriven;

  not not_1 (not_1_out, Addr[7]);
  ROM #(.AddrBits(8), .Bits(7)) rom_1 (.A({undriven[7], Addr[6:0]}), .sel(not_1_out), .D(D_out[6:0]));
  RAMDualPort ramdualport_1 (.A(Addr[1:0]), .Din(D_in), .str(str), .C(C), .ld(Addr[7]), .D(D_out[0]));
  // Pins of 2 and 7 and 8 bits meet at {undriven[7], Addr[6:0]}
  // Pins of 1 and 7 and 8 bits meet at D_out
  // Pins of 1 and 8 bits meet at Addr

  // Notes on the sheet:
  //   str: Enable RAM-Store
  //   C: Clock
endmodule
