// Digital circuit ProgramCounter.dig as structural Verilog
module ProgramCounter (
  input  [7:0] A_IN,
  input  INC,
  input  EN,
  input  CLK,
  input  RST,
  output [7:0] A_OUT
);

  wire not_1_out;
  wire [7:0] _8_bit_alu_1_out, multiplexer_1_out;

  not not_1 (not_1_out, INC);
  Multiplexer #(.Bits(8)) multiplexer_1 (
    .sel(not_1_out), .in_0(_8_bit_alu_1_out), .in_1(A_IN), .out(multiplexer_1_out));
  _8_Bit_Register _8_bit_register_1 (.RST(RST), .EN(EN), .D_in(multiplexer_1_out), .CLK(CLK), .D_out(A_OUT));
  _8_Bit_ALU _8_bit_alu_1 (
    .INVA(1'b0), .A(A_OUT), .ENA(1'b1), .B({8{1'b0}}), .ENB(1'b0), .C_IN(1'b1), .F0(1'b1), .F1(1'b1),
    .OUT(_8_bit_alu_1_out));  // open: C_OUT
endmodule
