// Digital circuit 1-Bit-ALU.dig as structural Verilog
module _1_Bit_ALU (
  input  INVA,
  input  A,
  input  ENA,
  input  B,
  input  ENB,
  input  C_IN,
  input  F0,
  input  F1,
  output C_OUT,
  output OUT
);

  wire and_1_out, and_2_out, and_3_out, and_4_out, and_5_out, and_6_out, and_7_out, and_8_out, and_9_out,
       and_10_out, and_11_out, and_12_out, and_13_out, not_1_out, or_1_out, xor_1_out, xor_2_out, xor_3_out;

  and and_1 (and_1_out, ~F0, ~F1);  // And
  and and_2 (and_2_out, ~F0, F1);  // And
  and and_3 (and_3_out, F0, ~F1);  // And
  and and_4 (and_4_out, F0, F1);
  and and_5 (and_5_out, A, ENA);
  and and_6 (and_6_out, B, ENB);
  xor xor_1 (xor_1_out, INVA, and_5_out);
  and and_7 (and_7_out, xor_1_out, and_6_out);
  or or_1 (or_1_out, xor_1_out, and_6_out);
  not not_1 (not_1_out, and_6_out);
  and and_8 (and_8_out, and_7_out, and_1_out);
  and and_9 (and_9_out, or_1_out, and_2_out);
  and and_10 (and_10_out, not_1_out, and_3_out);
  xor xor_2 (xor_2_out, and_6_out, xor_1_out);
  and and_11 (and_11_out, and_6_out, xor_1_out, and_4_out);
  xor xor_3 (xor_3_out, C_IN, xor_2_out);
  and and_12 (and_12_out, C_IN, xor_2_out, and_4_out);
  and and_13 (and_13_out, xor_3_out, and_4_out);
  or or_2 (C_OUT, and_12_out, and_11_out);
  or or_3 (OUT, and_8_out, and_9_out, and_10_out, and_13_out);

  // Notes on the sheet:
  //   ENA: Enable A
  //   ENB: Enable B
  //   C_IN: Carry input
  //   C_OUT: Output of the carry bit
  //   OUT: Output
  //   (Pipe at the beginning is needed, as DigitalOE strips whitespace at the front)
  //   |F0 | F1
  //   |  0 | 0   - AND
  //   |  0 | 1   - OR
  //   |  1 | 0   - NOT (Only Input-B)
  //   |  1 | 1   - Add (Full-Adder, A, B and Carry)
endmodule
