// Digital circuit 8-Bit-Register.dig as structural Verilog
module _8_Bit_Register (
  input  RST,
  input  EN,
  input  [7:0] D_in,
  input  CLK,
  output [7:0] D_out
);

  wire and_1_out;

  and and_1 (and_1_out, CLK, EN);
  D_FF_AS d_ff_as_1 (.Set(1'b0), .D(D_in[0]), .C(and_1_out), .Clr(RST), .Q(D_out[0]));  // open: nQ
  D_FF_AS d_ff_as_2 (.Set(1'b0), .D(D_in[1]), .C(and_1_out), .Clr(RST), .Q(D_out[1]));  // open: nQ
  D_FF_AS d_ff_as_3 (.Set(1'b0), .D(D_in[2]), .C(and_1_out), .Clr(RST), .Q(D_out[2]));  // open: nQ
  D_FF_AS d_ff_as_4 (.Set(1'b0), .D(D_in[3]), .C(and_1_out), .Clr(RST), .Q(D_out[3]));  // open: nQ
  D_FF_AS d_ff_as_5 (.Set(1'b0), .D(D_in[4]), .C(and_1_out), .Clr(RST), .Q(D_out[4]));  // open: nQ
  D_FF_AS d_ff_as_6 (.Set(1'b0), .D(D_in[5]), .C(and_1_out), .Clr(RST), .Q(D_out[5]));  // open: nQ
  D_FF_AS d_ff_as_7 (.Set(1'b0), .D(D_in[6]), .C(and_1_out), .Clr(RST), .Q(D_out[6]));  // open: nQ
  D_FF_AS d_ff_as_8 (.Set(1'b0), .D(D_in[7]), .C(and_1_out), .Clr(RST), .Q(D_out[7]));  // open: nQ

  // Notes on the sheet:
  //   RST: Reset
  //   EN: Enable
  //   D_in: Bussy_in
  //   CLK: Clock
  //   D_out: Output Bussy
  //   Cock'
  //   (Enable Logik)
endmodule
