// Digital circuit Komplettrechner.dig as structural Verilog
module Komplettrechner (
  input  Clock,
  input  RST
);

  wire ALU_c_out, C, not_1_out, Steuerwerk_adrmux, Steuerwerk_akku_en, Steuerwerk_alu_carry,
       Steuerwerk_execute, Steuerwerk_fetch_ar, Steuerwerk_fetch_ir, Steuerwerk_pc_en, Steuerwerk_pc_inc,
       Steuerwerk_ram_w;
  wire [4:0] Steuerwerk_alu_ctrl;
  wire [7:0] Akku_d_out, ALU_out, AR_d_out, IR_d_out, multiplexer_1_out, PC_a_out, ROM_d;

  STW Steuerwerk (
    .INSTR(IR_d_out), .CLK(C), .RST(RST), .FETCH_IR(Steuerwerk_fetch_ir), .FETCH_AR(Steuerwerk_fetch_ar),
    .EXECUTE(Steuerwerk_execute), .ALU_CTRL(Steuerwerk_alu_ctrl), .ALU_Carry(Steuerwerk_alu_carry),
    .Akku_EN(Steuerwerk_akku_en), .PC_INC(Steuerwerk_pc_inc), .PC_EN(Steuerwerk_pc_en),
    .ADRMUX(Steuerwerk_adrmux), .RAM_W(Steuerwerk_ram_w));
  and and_1 (C, Clock, ~RST);  // And
  _8_Bit_Register IR (.RST(RST), .EN(Steuerwerk_fetch_ir), .D_in(ROM_d), .CLK(C), .D_out(IR_d_out));
  LED led_1 (.in(Steuerwerk_fetch_ir));
  LED led_2 (.in(Steuerwerk_fetch_ar));
  LED led_3 (.in(Steuerwerk_execute));
  // Probe on IR_d_out
  _8_Bit_Register AR (.RST(RST), .EN(Steuerwerk_fetch_ar), .D_in(ROM_d), .CLK(C), .D_out(AR_d_out));
  ProgramCounter PC (
    .A_IN(AR_d_out), .INC(Steuerwerk_pc_inc), .EN(Steuerwerk_pc_en), .CLK(C), .RST(RST), .A_OUT(PC_a_out));
  // Probe on AR_d_out
  // Probe on PC_a_out
  ALU_Bus ALU (
    .CTRL(Steuerwerk_alu_ctrl), .A(ROM_d), .B(Akku_d_out), .C_IN(Steuerwerk_alu_carry), .OUT(ALU_out),
    .C_OUT(ALU_c_out));
  Multiplexer #(.Bits(8)) multiplexer_1 (
    .sel(Steuerwerk_adrmux), .in_0(AR_d_out), .in_1(PC_a_out), .out(multiplexer_1_out));
  // Probe on Steuerwerk_alu_ctrl
  not not_1 (not_1_out, multiplexer_1_out[7]);
  _8_Bit_Register Akku (.RST(RST), .EN(Steuerwerk_akku_en), .D_in(ALU_out), .CLK(C), .D_out(Akku_d_out));
  // Probe on Akku_d_out
  ROM #(.AddrBits(7), .Bits(8)) ROM (.A(multiplexer_1_out[6:0]), .sel(not_1_out), .D(ROM_d));
  RAMDualPort #(.AddrBits(7), .Bits(8)) RAM (
    .A(multiplexer_1_out[6:0]), .Din(Akku_d_out), .str(Steuerwerk_ram_w), .C(C), .ld(multiplexer_1_out[7]),
    .D(ROM_d));
  // Probe on Akku_d_out
  // Probe on ROM_d

  // Notes on the sheet:
  //   RST: Reset
  //   Speicher
  //   contents of ROM (hex, n*v repeats v):
  //   18,0,1e,10,80,80,a0,2,0,0,0,0,0,0,0,0,1
endmodule
