// Digital circuit SEQ.dig as structural Verilog
module SEQ (
  input  CLK,
  input  RST,
  output FETCH_IR,
  output FETCH_DR,
  output EXECUTE
);

  wire and_1_out, d_ff_as_1_q, q_0_q;

  and and_1 (and_1_out, ~d_ff_as_1_q, ~q_0_q);  // And
  D_FF_AS q_0 (.Set(1'b0), .D(and_1_out), .C(CLK), .Clr(RST), .Q(q_0_q));  // open: nQ
  D_FF_AS d_ff_as_1 (.Set(1'b0), .D(q_0_q), .C(CLK), .Clr(RST), .Q(d_ff_as_1_q));  // open: nQ
  and and_2 (FETCH_IR, ~q_0_q, ~d_ff_as_1_q);  // And
  and and_3 (FETCH_DR, q_0_q, ~d_ff_as_1_q);  // And
  and and_4 (EXECUTE, ~q_0_q, d_ff_as_1_q);  // And

  // Notes on the sheet:
  //   CLK: default 1
endmodule
