// Digital circuit TGI.dig as structural Verilog
module TGI (
  input  S,
  input  R,
  input  S_2,
  input  R_2,
  input  Clock,
  input  T,
  input  Clock_2,
  output Q,
  output Q_2,
  output Q_3,
  output Q_4,
  output Q_5,
  output Q_6
);

  wire and_1_out, and_2_out, and_3_out, xor_1_out;

  xor xor_1 (xor_1_out, Q_5, T);
  and and_1 (and_1_out, xor_1_out, Clock_2);
  nand nand_1 (Q_5, ~and_1_out, Q_6);  // NAnd
  nand nand_2 (Q_6, Q_5, and_1_out);
  and and_2 (and_2_out, S_2, Clock);
  and and_3 (and_3_out, Clock, R_2);
  nand nand_3 (Q, ~S, Q_2);  // NAnd
  nand nand_4 (Q_2, Q, ~R);  // NAnd
  nand nand_5 (Q_3, ~and_2_out, Q_4);  // NAnd
  nand nand_6 (Q_4, Q_3, ~and_3_out);  // NAnd

  // Notes on the sheet:
  //   T-FlipFlop
  //   Aufgabe 0
  //   Aufgabe 1
endmodule
